// Logisim project Practica1.circ as structural Verilog: 1 circuit, main circuit main
module main (
  input  in_1,
  input  in_2,
  input  in_3,
  input  in_4,
  input  in_5,
  input  in_6,
  input  in_7,
  input  in_8,
  input  in_9,
  input  in_10,
  input  in_11,
  input  in_12,
  input  in_13,
  input  in_14,
  input  in_15,
  input  in_16,
  input  in_17,
  input  in_18,
  input  in_19
);

  wire and_1_out, and_2_out, and_3_out, and_4_out, and_5_out, and_6_out, nand_1_out, nand_2_out, nand_3_out,
       nor_1_out, nor_2_out, nor_3_out, nor_4_out, not_1_out, not_2_out, not_3_out, not_4_out, not_5_out,
       not_6_out, not_7_out, not_8_out, not_9_out, not_10_out, not_11_out, not_12_out, not_13_out,
       not_14_out, or_1_out, or_2_out;

  not not_1 (not_1_out, in_6);
  not not_2 (not_2_out, in_11);
  not not_3 (not_3_out, in_13);
  not not_4 (not_4_out, in_14);
  not not_5 (not_5_out, in_15);
  not not_6 (not_6_out, in_16);
  not not_7 (not_7_out, in_17);
  not not_8 (not_8_out, in_18);
  not not_9 (not_9_out, in_19);
  nor nor_1 (nor_1_out, in_1, in_3);
  nor nor_2 (nor_2_out, in_3, not_1_out);
  or or_1 (or_1_out, in_9, not_2_out);
  nand nand_1 (nand_1_out, not_3_out, in_14);
  nand nand_2 (nand_2_out, not_4_out, not_5_out);
  and and_1 (and_1_out, in_18, in_19);
  and and_2 (and_2_out, not_8_out, not_9_out);
  nand nand_3 (nand_3_out, nor_1_out, nor_2_out);
  and and_3 (and_3_out, in_7, or_1_out);
  LED led_1 (.in(and_3_out));
  not not_10 (not_10_out, nand_1_out);
  not not_11 (not_11_out, nand_2_out);
  not not_12 (not_12_out, not_7_out);
  LED led_2 (.in(nand_3_out));
  or or_2 (or_2_out, not_10_out, not_11_out, not_6_out, not_12_out);
  LED led_3 (.in(or_2_out));
  nor nor_3 (nor_3_out, and_1_out, and_2_out);
  LED led_4 (.in(nor_3_out));
  not not_13 (not_13_out, in_2);
  and and_4 (and_4_out, in_4, in_5);
  not not_14 (not_14_out, in_12);
  nor nor_4 (nor_4_out, not_13_out, and_4_out);
  and and_5 (and_5_out, in_8, in_10, not_14_out);
  LED led_5 (.in(and_5_out));
  and and_6 (and_6_out, nor_4_out, in_2, in_4);
  LED led_6 (.in(and_6_out));
endmodule
