// Logisim project Suma.circ as structural Verilog: 2 circuits, main circuit main
module main (
  input  in_1,
  input  in_2,
  input  in_3,
  input  in_4,
  input  in_5,
  input  in_6,
  input  in_7,
  input  in_8,
  input  in_9,
  input  in_10,
  output out_11,
  output out_12,
  output out_13,
  output out_14,
  output out_15
);

  wire fa_2_cout, fa_3_cout, fa_4_cout, fa_5_cout;

  FA fa_1 (.A(in_2), .B(in_1), .C_IN(fa_2_cout), .S(out_11));  // open: Cout
  FA fa_2 (.A(in_4), .B(in_3), .C_IN(fa_3_cout), .S(out_12), .Cout(fa_2_cout));
  FA fa_3 (.A(in_6), .B(in_5), .C_IN(fa_4_cout), .S(out_13), .Cout(fa_3_cout));
  FA fa_4 (.A(in_8), .B(in_7), .C_IN(fa_5_cout), .S(out_14), .Cout(fa_4_cout));
  FA fa_5 (.A(in_10), .B(in_9), .S(out_15), .Cout(fa_5_cout));  // open: C_IN
endmodule

module FA (
  input  A,
  input  B,
  input  C_IN,
  output S,
  output Cout
);

  wire and_1_out, and_2_out, and_3_out, xor_1_out;

  xor xor_1 (xor_1_out, B, C_IN);
  and and_1 (and_1_out, A, B);
  and and_2 (and_2_out, B, C_IN);
  and and_3 (and_3_out, C_IN, A);
  xor xor_2 (S, A, xor_1_out);
  or or_1 (Cout, and_1_out, and_2_out, and_3_out);
endmodule
