// Logisim project Reloj.circ as structural Verilog: 1 circuit, main circuit main
module main (
);

  wire A1, a1_t, A2, a2_t, A3, a3_t, A4, a4_t, and_1_out, and_2_out, and_3_out, and_4_out, and_5_out,
       and_6_out, B1, b1_t, B2, b2_t, B3, b3_t, B4, b4_t, C1, c1_t, C2, c2_t, C3, c3_t, C4, c4_t, Carry1,
       Carry3, clock_1_out, Continue, CU, D1, d1_t, D2, d2_t, D3, d3_t, D4, d4_t, e1, e2, e3, e4, f1, f2, f3,
       f4, g1, g2, g3, g4, i, Increase, n74192_1_pin4, n74192_1_pin11, n74192_1_pin14, n74192_2_pin4,
       n74192_2_pin11, n74192_3_pin4, n74192_3_pin5, n74192_3_pin11, n74192_4_pin4, n74192_4_pin11, Set, st,
       t_ff_2_q, t_ff_2_qn;

  Button button_1 (.out(Continue));
  Button button_2 (.out(Set));
  Button button_3 (.out(Increase));
  _74192 #(.ShowInternalStructure("true")) u_74192_1 (
    .pin2(B1), .pin3(A1), .pin4(n74192_1_pin4), .pin5(CU), .pin6(C1), .pin7(D1), .pin14(n74192_1_pin14),
    .pin12(Carry1), .pin11(n74192_1_pin11));  // open: pin1, pin15, pin13, pin10, pin9
  _7447 #(.ShowInternalStructure("true")) u_7447_1 (
    .pin1(B1), .pin2(C1), .pin6(D1), .pin7(A1), .pin15(f1), .pin14(g1), .pin13(a1_t), .pin12(b1_t),
    .pin11(c1_t), .pin10(d1_t), .pin9(e1));  // open: pin3, pin4, pin5
  _7_Segment_Display #(.active("false"), .decimalPoint("false")) u_7_segment_display_1 (
    .g(g4), .f(f4), .a(a4_t), .b(b4_t), .e(e4), .d(d4_t), .c(c4_t));
  _7_Segment_Display #(.active("false"), .decimalPoint("false")) u_7_segment_display_2 (
    .g(g3), .f(f3), .a(a3_t), .b(b3_t), .e(e3), .d(d3_t), .c(c3_t));
  and and_1 (and_1_out, B2, C2);
  _74192 #(.ShowInternalStructure("true")) u_74192_2 (
    .pin2(B2), .pin3(A2), .pin4(n74192_2_pin4), .pin5(Carry1), .pin6(C2), .pin7(D2), .pin14(and_1_out),
    .pin11(n74192_2_pin11));  // open: pin1, pin15, pin13, pin12, pin10, pin9
  _7447 #(.ShowInternalStructure("true")) u_7447_2 (
    .pin1(B2), .pin2(C2), .pin6(D2), .pin7(A2), .pin15(f2), .pin14(g2), .pin13(a2_t), .pin12(b2_t),
    .pin11(c2_t), .pin10(d2_t), .pin9(e2));  // open: pin3, pin4, pin5
  _7_Segment_Display #(.active("false"), .decimalPoint("false")) u_7_segment_display_3 (
    .g(g2), .f(f2), .a(a2_t), .b(b2_t), .e(e2), .d(d2_t), .c(c2_t));
  and and_2 (and_2_out, C3, B4);
  _7_Segment_Display #(.active("false"), .decimalPoint("false")) u_7_segment_display_4 (
    .g(g1), .f(f1), .a(a1_t), .b(b1_t), .e(e1), .d(d1_t), .c(c1_t));
  _74192 #(.ShowInternalStructure("true")) u_74192_3 (
    .pin2(B3), .pin3(A3), .pin4(n74192_3_pin4), .pin5(n74192_3_pin5), .pin6(C3), .pin7(D3),
    .pin14(and_2_out), .pin12(Carry3), .pin11(n74192_3_pin11));  // open: pin1, pin15, pin13, pin10, pin9
  _7447 #(.ShowInternalStructure("true")) u_7447_3 (
    .pin1(B3), .pin2(C3), .pin6(D3), .pin7(A3), .pin15(f3), .pin14(g3), .pin13(a3_t), .pin12(b3_t),
    .pin11(c3_t), .pin10(d3_t), .pin9(e3));  // open: pin3, pin4, pin5
  or or_1 (n74192_3_pin5, i, and_3_out);
  and and_3 (and_3_out, B2, st, C2);
  T_Flip_Flop t_ff_1 (.Q(st), .reset(Set), .preset(Continue));  // open: T, clk, Qn
  T_Flip_Flop t_ff_2 (.T(Set), .clk(Set), .Q(t_ff_2_q), .Qn(t_ff_2_qn), .reset(Continue));  // open: preset
  and and_4 (and_4_out, C3, B4);
  _74192 #(.ShowInternalStructure("true")) u_74192_4 (
    .pin2(B4), .pin3(A4), .pin4(n74192_4_pin4), .pin5(Carry3), .pin6(C4), .pin7(D4), .pin14(and_4_out),
    .pin11(n74192_4_pin11));  // open: pin1, pin15, pin13, pin12, pin10, pin9
  _7447 #(.ShowInternalStructure("true")) u_7447_4 (
    .pin1(B4), .pin2(C4), .pin6(D4), .pin7(A4), .pin15(f4), .pin14(g4), .pin13(a4_t), .pin12(b4_t),
    .pin11(c4_t), .pin10(d4_t), .pin9(e4));  // open: pin3, pin4, pin5
  Clock clock_1 (.out(clock_1_out));
  and and_5 (and_5_out, clock_1_out, st);
  and and_6 (and_6_out, t_ff_2_q, Increase);
  and and_7 (i, t_ff_2_qn, Increase);
  or or_2 (CU, and_5_out, and_6_out);
  // also tied to GND on the sheet: n74192_1_pin14
  // also tied to VCC on the sheet: {n74192_1_pin11, n74192_1_pin4, n74192_2_pin11, n74192_2_pin4, n74192_3_pin11, n74192_3_pin4, n74192_4_pin11, n74192_4_pin4}

  // Notes on the sheet:
  //   load
  //   clear
  //   load
  //   load
  //   load
endmodule
